# Fritzing sketch TransmitterCircuitDiagram (saved by Fritzing 0.7.12b)
breadboards: 1

parts:
  Arduino1 = Arduino
  VCC1 = Battery  # not connected
  RFM12b1 = RFM12b HopeRF Transceiver

nets:
  N1: Arduino1.GND, RFM12b1.10_GND
  N2: Arduino1.D1TX, RFM12b1.5_CLK
  N3: Arduino1.+5V, RFM12b1.9_VDD
